// Logisim project control-logic.circ as structural Verilog: 1 circuit, main circuit control_logic
module control_logic (
  input  [31:0] Instruction,
  input  BrEq,
  input  BrLt,
  output PCSel,
  output RegWEn,
  output [2:0] ImmSel,
  output BrUn,
  output ASel,
  output BSel,
  output [3:0] ALUSel,
  output MemWEn,
  output [1:0] WBSel
);

  wire and_1_out, and_2_out, and_3_out, and_12_out, and_13_out, and_17_out, comparator_1_eq, comparator_2_eq,
       comparator_3_eq, comparator_4_eq, comparator_5_eq, comparator_6_eq, comparator_8_eq, comparator_9_eq,
       comparator_10_eq, comparator_11_eq, comparator_12_eq, comparator_13_eq, comparator_14_eq,
       comparator_15_eq, comparator_16_eq, comparator_17_eq, comparator_18_eq, comparator_19_eq,
       comparator_20_eq, comparator_22_eq, comparator_23_eq, comparator_24_eq, comparator_25_eq,
       comparator_26_eq, comparator_27_eq, comparator_28_eq, is_add, is_addi, is_and, is_andi, is_I_type,
       is_mul, is_mulh, is_mulhu, is_or, is_ori, is_R_type, is_sll, is_slli, is_slt, is_slti, is_sra,
       is_srai, is_srl, is_srli, is_sub, is_xor, is_xori;
  wire [5:0] ROMInput;
  wire [15:14] rom_1_data;

  ROM #(.addrWidth(6), .dataWidth(16)) rom_1 (
    .addr(ROMInput), .data({rom_1_data, WBSel, MemWEn, ALUSel, BSel, ASel, BrUn, ImmSel, RegWEn}));
  Priority_Encoder #(.select_enc(6)) priority_encoder_1 (
    .in0(is_add), .in1(is_mul), .in2(is_sub), .in3(is_sll), .in4(is_mulh), .in5(is_mulhu), .in6(is_slt),
    .in7(is_xor), .in8(is_srl), .in9(is_sra), .in10(is_or), .in11(is_and), .in15(is_addi), .in16(is_slli),
    .in17(is_slti), .in18(is_xori), .in19(is_srli), .in20(is_srai), .in21(is_ori), .in22(is_andi),
    .out(ROMInput));  // open: in12, in13, in14, in23, in24, in25, in26, in27, in28, in29, in30, in31, in32, in33, in34, in35, in36, in37, in38, in39, in40, in41, in42, in43, in44, in45, in46, in47, in48, in49, in50, in51, in52, in53, in54, in55, in56, in57, in58, in59, in60, in61, in62, in63, gs, en_out, en_in
  Comparator #(.width(3)) comparator_1 (.a(3'b001), .b(Instruction[14:12]), .eq(comparator_1_eq));  // open: gt, lt
  Comparator #(.width(3)) comparator_2 (.a(3'b101), .b(Instruction[14:12]), .eq(comparator_2_eq));  // open: gt, lt
  Comparator #(.width(3)) comparator_3 (.a(3'b101), .b(Instruction[14:12]), .eq(comparator_3_eq));  // open: gt, lt
  Comparator #(.width(7)) comparator_4 (.a({7{1'b0}}), .b(Instruction[31:25]), .eq(comparator_4_eq));  // open: gt, lt
  and and_1 (and_1_out, is_I_type, comparator_1_eq);
  Comparator #(.width(7)) comparator_5 (.a({7{1'b0}}), .b(Instruction[31:25]), .eq(comparator_5_eq));  // open: gt, lt
  and and_2 (and_2_out, is_I_type, comparator_2_eq);
  Comparator #(.width(7)) comparator_6 (.a(7'b0100000), .b(Instruction[31:25]), .eq(comparator_6_eq));  // open: gt, lt
  and and_3 (and_3_out, is_I_type, comparator_3_eq);
  Comparator #(.width(7)) comparator_7 (.a(7'b0010011), .b(Instruction[6:0]), .eq(is_I_type));  // open: gt, lt
  Comparator #(.width(3)) comparator_8 (.a(3'b000), .b(Instruction[14:12]), .eq(comparator_8_eq));  // open: gt, lt
  and and_4 (is_slli, comparator_4_eq, and_1_out);
  Comparator #(.width(3)) comparator_9 (.a(3'b010), .b(Instruction[14:12]), .eq(comparator_9_eq));  // open: gt, lt
  Comparator #(.width(3)) comparator_10 (.a(3'b100), .b(Instruction[14:12]), .eq(comparator_10_eq));  // open: gt, lt
  and and_5 (is_srli, comparator_5_eq, and_2_out);
  and and_6 (is_srai, comparator_6_eq, and_3_out);
  Comparator #(.width(3)) comparator_11 (.a(3'b110), .b(Instruction[14:12]), .eq(comparator_11_eq));  // open: gt, lt
  Comparator #(.width(3)) comparator_12 (.a(3'b111), .b(Instruction[14:12]), .eq(comparator_12_eq));  // open: gt, lt
  and and_7 (is_addi, is_I_type, comparator_8_eq);
  and and_8 (is_slti, is_I_type, comparator_9_eq);
  and and_9 (is_xori, is_I_type, comparator_10_eq);
  and and_10 (is_ori, is_I_type, comparator_11_eq);
  and and_11 (is_andi, is_I_type, comparator_12_eq);
  Comparator #(.width(3)) comparator_13 (.a(3'b000), .b(Instruction[14:12]), .eq(comparator_13_eq));  // open: gt, lt
  Comparator #(.width(3)) comparator_14 (.a(3'b001), .b(Instruction[14:12]), .eq(comparator_14_eq));  // open: gt, lt
  Comparator #(.width(3)) comparator_15 (.a(3'b010), .b(Instruction[14:12]), .eq(comparator_15_eq));  // open: gt, lt
  Comparator #(.width(3)) comparator_16 (.a(3'b011), .b(Instruction[14:12]), .eq(comparator_16_eq));  // open: gt, lt
  Comparator #(.width(3)) comparator_17 (.a(3'b100), .b(Instruction[14:12]), .eq(comparator_17_eq));  // open: gt, lt
  Comparator #(.width(3)) comparator_18 (.a(3'b101), .b(Instruction[14:12]), .eq(comparator_18_eq));  // open: gt, lt
  Comparator #(.width(3)) comparator_19 (.a(3'b110), .b(Instruction[14:12]), .eq(comparator_19_eq));  // open: gt, lt
  Comparator #(.width(3)) comparator_20 (.a(3'b111), .b(Instruction[14:12]), .eq(comparator_20_eq));  // open: gt, lt
  Comparator #(.width(7)) comparator_21 (.a(7'b0110011), .b(Instruction[6:0]), .eq(is_R_type));  // open: gt, lt
  Comparator #(.width(7)) comparator_22 (.a({7{1'b0}}), .b(Instruction[31:25]), .eq(comparator_22_eq));  // open: gt, lt
  and and_12 (and_12_out, is_R_type, comparator_13_eq);
  Comparator #(.width(7)) comparator_23 (
    .a(7'b0000001), .b(Instruction[31:25]), .eq(comparator_23_eq));  // open: gt, lt
  Comparator #(.width(7)) comparator_24 (
    .a(7'b0100000), .b(Instruction[31:25]), .eq(comparator_24_eq));  // open: gt, lt
  Comparator #(.width(7)) comparator_25 (.a({7{1'b0}}), .b(Instruction[31:25]), .eq(comparator_25_eq));  // open: gt, lt
  and and_13 (and_13_out, is_R_type, comparator_14_eq);
  and and_14 (is_slt, is_R_type, comparator_15_eq);
  and and_15 (is_mulhu, is_R_type, comparator_16_eq);
  and and_16 (is_xor, is_R_type, comparator_17_eq);
  Comparator #(.width(7)) comparator_26 (.a({7{1'b0}}), .b(Instruction[31:25]), .eq(comparator_26_eq));  // open: gt, lt
  and and_17 (and_17_out, is_R_type, comparator_18_eq);
  and and_18 (is_or, is_R_type, comparator_19_eq);
  and and_19 (is_and, is_R_type, comparator_20_eq);
  and and_20 (is_add, comparator_22_eq, and_12_out);
  and and_21 (is_mul, and_12_out, comparator_23_eq);
  and and_22 (is_sub, and_12_out, comparator_24_eq);
  Comparator #(.width(7)) comparator_27 (
    .a(7'b0000001), .b(Instruction[31:25]), .eq(comparator_27_eq));  // open: gt, lt
  Comparator #(.width(7)) comparator_28 (
    .a(7'b0100000), .b(Instruction[31:25]), .eq(comparator_28_eq));  // open: gt, lt
  and and_23 (is_sll, comparator_25_eq, and_13_out);
  and and_24 (is_mulh, and_13_out, comparator_27_eq);
  and and_25 (is_srl, comparator_26_eq, and_17_out);
  and and_26 (is_sra, and_17_out, comparator_28_eq);

  assign PCSel = 1'b0;

  // Other names for the same wires on the sheet: opcode[6:0] = Instruction[6:0]; func3[2:0] = Instruction[14:12]

  // Notes on the sheet:
  //   INPUTS to your circuit
  //   contents of rom_1 (hex, n*v repeats v):
  //   1001 1401 1601 1081 1481 1581 1101 1201 1281 1681 1301 1381 41 41 41 1041 10c1 1141 1241 12c1 16c1
  //   1341 13c1 1842 1842 1842 4*1064 1074 1074 1067 17c7 2069 2041
  //   ROM FOR CONTROL LOGIC
  //   DON'T CHANGE THE LOCATIONS OF THE INPUTS AND OUTPUTS!
  //   This is only if you choose to do the ROM option
  //   CONNECT
  //   WIRE
  //   TO
  //   USE
  //   ROM
  //   OUTPUT from your circuit
  //   Reminder: If using ROM, use combinational logic for PCSel
  //   I-Type
  //   R-Type
endmodule
