// Logisim project imm-gen.circ as structural Verilog: 1 circuit, main circuit imm_gen
module imm_gen (
  input  [31:0] Instruction,
  input  [2:0] ImmSel,
  output [31:0] Immediate
);

  wire [31:0] adder_1_out, adder_2_out, B_imme, bit_extender_1_out, bit_extender_2_out, bit_extender_3_out,
       bit_extender_4_out, I_imme, shifter_1_out, shifter_2_out, shifter_3_out, shifter_4_out;

  assign bit_extender_1_out = {{31{1'b0}}, Instruction[7]};  // Bit_Extender bit_extender_1
  assign bit_extender_2_out = {{28{1'b0}}, Instruction[11:8]};  // Bit_Extender bit_extender_2
  assign bit_extender_3_out = {{26{1'b0}}, Instruction[30:25]};  // Bit_Extender bit_extender_3
  assign bit_extender_4_out = {{31{Instruction[31]}}, Instruction[31]};  // Bit_Extender bit_extender_4
  Multiplexer #(.select(3), .width(32)) multiplexer_1 (
    .in0(I_imme), .in2(B_imme), .out(Immediate), .sel(ImmSel));  // open: in1, in3, in4, in5, in6, in7
  assign I_imme = {{20{Instruction[31]}}, Instruction[31:20]};  // Bit_Extender bit_extender_5
  Shifter #(.width(32)) shifter_1 (.in(bit_extender_1_out), .\dist (5'b01011), .out(shifter_1_out));
  Shifter #(.width(32)) shifter_2 (.in(bit_extender_2_out), .\dist (5'b00001), .out(shifter_2_out));
  Shifter #(.width(32)) shifter_3 (.in(bit_extender_3_out), .\dist (5'b00101), .out(shifter_3_out));
  Shifter #(.width(32)) shifter_4 (.in(bit_extender_4_out), .\dist (5'b01100), .out(shifter_4_out));
  Adder #(.width(32)) adder_1 (.a(shifter_1_out), .b(shifter_2_out), .out(adder_1_out));  // open: cin, cout
  Adder #(.width(32)) adder_2 (.a(shifter_3_out), .b(shifter_4_out), .out(adder_2_out));  // open: cin, cout
  Adder #(.width(32)) adder_3 (.a(adder_1_out), .b(adder_2_out), .out(B_imme));  // open: cin, cout

  // Notes on the sheet:
  //   INPUTS to your circuit
  //   DON'T CHANGE THE LOCATIONS OF THE INPUTS AND OUTPUTS!
  //   OUTPUT from your circuit
endmodule
